// Logisim project ecuacion.circ as structural Verilog: 1 circuit, main circuit Ecuacion ax+b
module Ecuacion_ax_b (
  input  A1,
  input  A0,
  input  X1,
  input  X0,
  input  B1,
  input  B0,
  output Y2,
  output Y1,
  output Y0
);

  wire and_1_out, and_2_out, and_3_out, and_4_out, and_5_out, and_6_out, and_7_out, and_8_out, and_9_out,
       and_10_out, and_11_out, and_12_out, or_1_out, or_2_out, or_3_out, or_4_out, or_5_out,
       transistor_1_out, transistor_3_out;

  and and_1 (and_1_out, A1, ~X1, X0);  // AND_Gate
  and and_2 (and_2_out, ~A1, A0, X1);  // AND_Gate
  and and_3 (and_3_out, A0, X0);
  Transistor #(.\type ("n")) transistor_1 (.in(1'b1), .out(transistor_1_out), .gate(or_1_out));
  or or_1 (or_1_out, and_1_out, and_2_out);
  Transistor transistor_2 (.in(1'b0), .out(transistor_1_out), .gate(or_1_out));
  Transistor #(.\type ("n")) transistor_3 (.in(1'b1), .out(transistor_3_out), .gate(and_3_out));
  Transistor transistor_4 (.in(1'b0), .out(transistor_3_out), .gate(and_3_out));
  and and_4 (and_4_out, transistor_1_out, B1);
  and and_5 (and_5_out, transistor_1_out, ~B1, ~B0);  // AND_Gate
  and and_6 (and_6_out, ~B1, transistor_1_out, ~transistor_3_out);  // AND_Gate
  and and_7 (and_7_out, B1, ~transistor_1_out, ~transistor_3_out);  // AND_Gate
  and and_8 (and_8_out, ~transistor_1_out, B1, ~B0);  // AND_Gate
  and and_9 (and_9_out, ~transistor_1_out, transistor_3_out, ~B1, B0);  // AND_Gate
  and and_10 (and_10_out, transistor_3_out, transistor_1_out, B1, B0);
  and and_11 (and_11_out, transistor_3_out, ~B0);  // AND_Gate
  and and_12 (and_12_out, B0, ~transistor_3_out);  // AND_Gate
  or or_2 (or_2_out, and_5_out, and_6_out, and_7_out, and_8_out);
  or or_3 (or_3_out, and_11_out, and_12_out);
  Transistor #(.\type ("n")) transistor_5 (.in(1'b1), .out(Y2), .gate(or_4_out));
  or or_4 (or_4_out, and_4_out, or_2_out);
  Transistor transistor_6 (.in(1'b0), .out(Y2), .gate(or_4_out));
  Transistor #(.\type ("n")) transistor_7 (.in(1'b1), .out(Y1), .gate(or_5_out));
  or or_5 (or_5_out, or_2_out, and_9_out, and_10_out);
  Transistor transistor_8 (.in(1'b0), .out(Y1), .gate(or_5_out));
  Transistor #(.\type ("n")) transistor_9 (.in(1'b1), .out(Y0), .gate(or_3_out));
  Transistor transistor_10 (.in(1'b0), .out(Y0), .gate(or_3_out));
endmodule
