// Logisim project multi2bits.circ as structural Verilog: 1 circuit, main circuit Multiplicacion-2bits
module Multiplicacion_2bits (
  input  A1,
  input  A0,
  input  B1,
  input  B0,
  output C1,
  output C0
);

  wire and_1_out, and_2_out, and_3_out, or_1_out;

  and and_1 (and_1_out, A1, ~B1, B0);  // AND_Gate
  or or_1 (or_1_out, and_1_out, and_2_out);
  and and_2 (and_2_out, ~A1, A0, B1);  // AND_Gate
  and and_3 (and_3_out, A0, B0);
  Transistor #(.\type ("n")) transistor_1 (.in(1'b1), .out(C1), .gate(or_1_out));
  Transistor transistor_2 (.in(1'b0), .out(C1), .gate(or_1_out));
  Transistor #(.\type ("n")) transistor_3 (.in(1'b1), .out(C0), .gate(and_3_out));
  Transistor transistor_4 (.in(1'b0), .out(C0), .gate(and_3_out));
endmodule
