// Logisim project multi4bits.circ as structural Verilog: 1 circuit, main circuit Multiplicacion-4bits
module Multiplicacion_4bits (
  input  A1,
  input  A0,
  input  B1,
  input  B0,
  output C3,
  output C2,
  output C1,
  output C0
);

  wire and_1_out, and_2_out, and_3_out, and_4_out, and_5_out, and_6_out, or_1_out, or_2_out, or_3_out,
       or_4_out;

  and and_1 (and_1_out, A1, ~B1, B0);  // AND_Gate
  and and_2 (and_2_out, ~A1, A0, B1);  // AND_Gate
  and and_3 (and_3_out, A1, ~A0, B1, ~B0);  // AND_Gate
  and and_4 (and_4_out, A1, ~A0, B0);  // AND_Gate
  and and_5 (and_5_out, A0, B1, ~B0);  // AND_Gate
  and and_6 (and_6_out, A0, B0);
  or or_1 (or_1_out, and_1_out, and_2_out);
  or or_2 (or_2_out, or_1_out, and_3_out);
  or or_3 (or_3_out, or_1_out, or_4_out);
  or or_4 (or_4_out, and_4_out, and_5_out);
  Transistor #(.\type ("n"), .gate("br")) transistor_1 (.in(1'b1), .out(C3), .gate(or_1_out));
  Transistor #(.gate("br")) transistor_2 (.in(1'b0), .out(C3), .gate(or_1_out));
  Transistor #(.\type ("n"), .gate("br")) transistor_3 (.in(1'b1), .out(C2), .gate(or_2_out));
  Transistor #(.gate("br")) transistor_4 (.in(1'b0), .out(C2), .gate(or_2_out));
  Transistor #(.\type ("n"), .gate("br")) transistor_5 (.in(1'b1), .out(C1), .gate(or_3_out));
  Transistor #(.gate("br")) transistor_6 (.in(1'b0), .out(C1), .gate(or_3_out));
  Transistor #(.gate("br")) transistor_7 (.in(1'b0), .out(C0), .gate(and_6_out));
  Transistor #(.\type ("n"), .gate("br")) transistor_8 (.in(1'b1), .out(C0), .gate(and_6_out));
endmodule
