// Logisim project suma.circ as structural Verilog: 1 circuit, main circuit Suma
module Suma (
  input  A1,
  input  A0,
  input  B1,
  input  B0,
  output C2,
  output C1,
  output C0
);

  wire and_1_out, and_2_out, and_3_out, and_4_out, and_5_out, and_6_out, and_7_out, and_8_out, and_9_out,
       or_1_out, or_2_out, or_3_out, or_4_out;

  and and_1 (and_1_out, A1, B1);
  and and_2 (and_2_out, A1, ~B1, ~B0);  // AND_Gate
  and and_3 (and_3_out, ~B1, A1, ~A0);  // AND_Gate
  and and_4 (and_4_out, B1, ~A1, ~A0);  // AND_Gate
  and and_5 (and_5_out, ~A1, B1, ~B0);  // AND_Gate
  and and_6 (and_6_out, ~A1, A0, ~B1, B0);  // AND_Gate
  and and_7 (and_7_out, A0, A1, B1, B0);
  and and_8 (and_8_out, A0, ~B0);  // AND_Gate
  and and_9 (and_9_out, B0, ~A0);  // AND_Gate
  or or_1 (or_1_out, and_2_out, and_3_out, and_4_out, and_5_out);
  or or_2 (or_2_out, and_8_out, and_9_out);
  or or_3 (or_3_out, and_1_out, or_1_out);
  or or_4 (or_4_out, or_1_out, and_6_out, and_7_out);
  Transistor #(.\type ("n")) transistor_1 (.in(1'b1), .out(C2), .gate(or_3_out));
  Transistor transistor_2 (.in(1'b0), .out(C2), .gate(or_3_out));
  Transistor #(.\type ("n")) transistor_3 (.in(1'b1), .out(C1), .gate(or_4_out));
  Transistor transistor_4 (.in(1'b0), .out(C1), .gate(or_4_out));
  Transistor #(.\type ("n")) transistor_5 (.in(1'b1), .out(C0), .gate(or_2_out));
  Transistor transistor_6 (.in(1'b0), .out(C0), .gate(or_2_out));
endmodule
