// Logisim project secuencia10110traslape.circ as structural Verilog: 1 circuit, main circuit Moore 2
module Moore_2 (
);

  wire and_1_out, and_2_out, and_3_out, and_4_out, and_5_out, and_6_out, and_7_out, and_8_out, and_9_out,
       clock_1_out, E0_q, E0_qn, E1_q, E1_qn, E2_q, E2_qn, I_out, not_1_out, or_1_out, or_2_out, or_3_out;

  Button I (.out(I_out));
  not not_1 (not_1_out, I_out);
  D_Flip_Flop E2 (.clk(clock_1_out), .D(or_1_out), .Q(E2_q), .Qn(E2_qn));  // open: preset, en, reset
  and and_1 (and_1_out, E0_q, E1_q, I_out);
  and and_2 (and_2_out, E2_q, E0_qn, not_1_out);
  and and_3 (and_3_out, E0_q, not_1_out);
  and and_4 (and_4_out, E1_q, E0_qn, I_out);
  and and_5 (and_5_out, E2_q, E0_q, I_out);
  and and_6 (and_6_out, E1_qn, I_out);
  and and_7 (and_7_out, E0_qn, I_out);
  and and_8 (and_8_out, E2_q, E0_qn);
  D_Flip_Flop E1 (.clk(clock_1_out), .D(or_2_out), .Q(E1_q), .Qn(E1_qn));  // open: preset, en, reset
  Clock clock_1 (.out(clock_1_out));
  or or_1 (or_1_out, and_1_out, and_2_out);
  or or_2 (or_2_out, and_3_out, and_4_out, and_5_out);
  or or_3 (or_3_out, and_6_out, and_7_out, and_8_out);
  D_Flip_Flop E0 (.clk(clock_1_out), .D(or_3_out), .Q(E0_q), .Qn(E0_qn));  // open: preset, en, reset
  LED O (.in(and_9_out));
  and and_9 (and_9_out, E2_q, E0_q);
endmodule
